// Logisim project DigitSampleCirc.circ as structural Verilog: 1 circuit, main circuit DigitSample
module DigitSample (
  input  in_1,
  input  in_2,
  input  in_3,
  input  in_4,
  input  in_5,
  input  in_6,
  input  in_7,
  input  in_8
);

  _7_Segment_Display u_7_segment_display_1 (
    .g(in_8), .f(in_7), .a(in_6), .b(in_5), .e(in_4), .d(in_3), .c(in_2), .dp(in_1));

  // Notes on the sheet:
  //   9
  //   8
  //   7
  //   6
  //   5
  //   4
  //   3
  //   2
  //   1
  //   0
endmodule
