// Logisim project Display_Screen_Blackbox.circ as structural Verilog: 1 circuit, main circuit displayScreenBlackbox
module displayScreenBlackbox (
  input  MSBBit,
  input  Bit2,
  input  Bit1,
  input  LSBBit,
  output D1B0345,
  output D1B12,
  output D1B6,
  output D2B0,
  output D2B1,
  output D2B2,
  output D2B3,
  output D2B4,
  output D2B5,
  output D2B6
);

  wire and_1_out, Eight_out, Eleven_out, Fifteen_out, Five_out, Four_out, Fourteen_out, not_1_out, not_2_out,
       not_3_out, One_out, Seven_out, Six_out, Ten_out, Thirteen_out, Three_out, Twelve_out, Two_out,
       Zero_out;

  and Zero (Zero_out, ~MSBBit, ~Bit2, ~Bit1, ~LSBBit);  // AND_Gate
  and One (One_out, ~MSBBit, ~Bit2, ~Bit1, LSBBit);  // AND_Gate
  and Two (Two_out, ~MSBBit, ~Bit2, Bit1, ~LSBBit);  // AND_Gate
  and Three (Three_out, ~MSBBit, ~Bit2, Bit1, LSBBit);  // AND_Gate
  and Four (Four_out, ~MSBBit, Bit2, ~Bit1, ~LSBBit);  // AND_Gate
  and Five (Five_out, ~MSBBit, Bit2, ~Bit1, LSBBit);  // AND_Gate
  and Six (Six_out, ~MSBBit, Bit2, Bit1, ~LSBBit);  // AND_Gate
  and Seven (Seven_out, ~MSBBit, Bit2, Bit1, LSBBit);  // AND_Gate
  and Eight (Eight_out, MSBBit, ~Bit2, ~Bit1, ~LSBBit);  // AND_Gate
  // AND_Gate Nine has open pins: in0=MSBBit, in1=Bit2, in2=Bit1, in3=LSBBit, out=open
  and Ten (Ten_out, MSBBit, ~Bit2, Bit1, ~LSBBit);  // AND_Gate
  and Eleven (Eleven_out, MSBBit, ~Bit2, Bit1, LSBBit);  // AND_Gate
  and Twelve (Twelve_out, MSBBit, Bit2, ~Bit1, ~LSBBit);  // AND_Gate
  and Thirteen (Thirteen_out, MSBBit, Bit2, ~Bit1, LSBBit);  // AND_Gate
  and Fourteen (Fourteen_out, MSBBit, Bit2, Bit1, ~LSBBit);  // AND_Gate
  and Fifteen (Fifteen_out, MSBBit, Bit2, Bit1, LSBBit);
  not not_1 (not_1_out, Bit1);
  not not_2 (not_2_out, Bit2);
  and and_1 (and_1_out, not_1_out, not_2_out, MSBBit);
  not not_3 (not_3_out, MSBBit);
  not not_4 (D1B6, 1'b1);
  or or_1 (D1B0345, and_1_out, not_3_out);
  and and_2 (D2B0, ~One_out, ~Four_out, ~Eleven_out, ~Fourteen_out);  // AND_Gate
  and and_3 (D2B1, ~Five_out, ~Six_out, ~Fifteen_out);  // AND_Gate
  and and_4 (D2B2, ~Two_out, ~Twelve_out);  // AND_Gate
  and and_5 (D2B3, ~One_out, ~Four_out, ~Seven_out, ~Eleven_out, ~Fourteen_out);  // AND_Gate
  or or_2 (D2B4, Zero_out, Two_out, Six_out, Eight_out, Ten_out, Twelve_out);
  and and_6 (D2B5, ~One_out, ~Two_out, ~Three_out, ~Seven_out, ~Eleven_out, ~Twelve_out, ~Thirteen_out);  // AND_Gate
  and and_7 (D2B6, ~Zero_out, ~One_out, ~Seven_out, ~Ten_out, ~Eleven_out);  // AND_Gate

  assign D1B12 = 1'b1;
endmodule
