// Logisim project MicroCounterDraft.circ as structural Verilog: 1 circuit, main circuit MicroCounter
module MicroCounter (
  input  CounterClock,
  input  ResetToZero,
  output MicroZero,
  output MicroOne,
  output MicroTwo,
  output MicroThree,
  output MicroFour,
  output MicroFive,
  output MicroSix,
  output MicroSeven
);

  wire controlled_buffer_1_out, controlled_buffer_2_out, controlled_buffer_3_out, d_ff_1_q, d_ff_2_q,
       d_ff_3_q, FiveToSix_out, FourToFive_out, ModeAdd_out, ModeReset_out, not_1_out, not_2_out, not_3_out,
       not_4_out, not_5_out, not_6_out, not_7_out, not_8_out, not_9_out, not_10_out, not_11_out, not_12_out,
       not_13_out, OneToTwo_out, SevenToZero_out, SixToSeven_out, ThreeToFour_out, TwoToThree_out, undriven,
       undriven_2, ZeroToOne_out;

  not not_1 (not_1_out, ResetToZero);
  and ModeReset (ModeReset_out, CounterClock, ResetToZero);
  and ModeAdd (ModeAdd_out, CounterClock, not_1_out);
  assign controlled_buffer_1_out = ModeReset_out ? 1'b0 : 1'bz;  // Controlled_Buffer controlled_buffer_1
  assign controlled_buffer_2_out = ModeReset_out ? 1'b0 : 1'bz;  // Controlled_Buffer controlled_buffer_2
  assign controlled_buffer_3_out = ModeReset_out ? 1'b0 : 1'bz;  // Controlled_Buffer controlled_buffer_3
  and ZeroToOne (ZeroToOne_out, ModeAdd_out, MicroZero);
  assign controlled_buffer_3_out = ZeroToOne_out ? 1'b0 : 1'bz;  // Controlled_Buffer controlled_buffer_4
  assign controlled_buffer_2_out = ZeroToOne_out ? 1'b0 : 1'bz;  // Controlled_Buffer controlled_buffer_5
  assign controlled_buffer_1_out = ZeroToOne_out ? 1'b1 : 1'bz;  // Controlled_Buffer controlled_buffer_6
  and OneToTwo (OneToTwo_out, ModeAdd_out, MicroOne);
  assign controlled_buffer_3_out = OneToTwo_out ? 1'b0 : 1'bz;  // Controlled_Buffer controlled_buffer_7
  assign controlled_buffer_2_out = OneToTwo_out ? 1'b1 : 1'bz;  // Controlled_Buffer controlled_buffer_8
  assign controlled_buffer_1_out = OneToTwo_out ? 1'b0 : 1'bz;  // Controlled_Buffer controlled_buffer_9
  and TwoToThree (TwoToThree_out, ModeAdd_out, MicroTwo);
  D_Flip_Flop #(.trigger("falling")) d_ff_1 (
    .D(controlled_buffer_1_out), .clk(CounterClock), .Q(d_ff_1_q), .reset(undriven));  // open: Qn, preset
  D_Flip_Flop #(.trigger("falling")) d_ff_2 (
    .D(controlled_buffer_2_out), .clk(CounterClock), .Q(d_ff_2_q), .preset(undriven), .reset(undriven_2));  // open: Qn
  D_Flip_Flop #(.trigger("falling")) d_ff_3 (
    .D(controlled_buffer_3_out), .clk(CounterClock), .Q(d_ff_3_q), .preset(undriven_2));  // open: Qn, reset
  and ThreeToFour (ThreeToFour_out, ModeAdd_out, MicroThree);
  assign controlled_buffer_3_out = TwoToThree_out ? 1'b0 : 1'bz;  // Controlled_Buffer controlled_buffer_10
  assign controlled_buffer_2_out = TwoToThree_out ? 1'b1 : 1'bz;  // Controlled_Buffer controlled_buffer_11
  assign controlled_buffer_1_out = TwoToThree_out ? 1'b1 : 1'bz;  // Controlled_Buffer controlled_buffer_12
  and FourToFive (FourToFive_out, ModeAdd_out, MicroFour);
  assign controlled_buffer_3_out = ThreeToFour_out ? 1'b1 : 1'bz;  // Controlled_Buffer controlled_buffer_13
  assign controlled_buffer_2_out = ThreeToFour_out ? 1'b0 : 1'bz;  // Controlled_Buffer controlled_buffer_14
  assign controlled_buffer_1_out = ThreeToFour_out ? 1'b0 : 1'bz;  // Controlled_Buffer controlled_buffer_15
  assign controlled_buffer_3_out = FourToFive_out ? 1'b1 : 1'bz;  // Controlled_Buffer controlled_buffer_16
  assign controlled_buffer_2_out = FourToFive_out ? 1'b0 : 1'bz;  // Controlled_Buffer controlled_buffer_17
  assign controlled_buffer_1_out = FourToFive_out ? 1'b1 : 1'bz;  // Controlled_Buffer controlled_buffer_18
  and FiveToSix (FiveToSix_out, ModeAdd_out, MicroFive);
  assign controlled_buffer_3_out = FiveToSix_out ? 1'b1 : 1'bz;  // Controlled_Buffer controlled_buffer_19
  assign controlled_buffer_2_out = FiveToSix_out ? 1'b1 : 1'bz;  // Controlled_Buffer controlled_buffer_20
  assign controlled_buffer_1_out = FiveToSix_out ? 1'b0 : 1'bz;  // Controlled_Buffer controlled_buffer_21
  and SixToSeven (SixToSeven_out, ModeAdd_out, MicroSix);
  assign controlled_buffer_3_out = SixToSeven_out ? 1'b1 : 1'bz;  // Controlled_Buffer controlled_buffer_22
  assign controlled_buffer_2_out = SixToSeven_out ? 1'b1 : 1'bz;  // Controlled_Buffer controlled_buffer_23
  assign controlled_buffer_1_out = SixToSeven_out ? 1'b1 : 1'bz;  // Controlled_Buffer controlled_buffer_24
  and SevenToZero (SevenToZero_out, ModeAdd_out, MicroSeven);
  assign controlled_buffer_3_out = SevenToZero_out ? 1'b0 : 1'bz;  // Controlled_Buffer controlled_buffer_25
  assign controlled_buffer_2_out = SevenToZero_out ? 1'b0 : 1'bz;  // Controlled_Buffer controlled_buffer_26
  assign controlled_buffer_1_out = SevenToZero_out ? 1'b0 : 1'bz;  // Controlled_Buffer controlled_buffer_27
  and Seven (MicroSeven, d_ff_3_q, d_ff_2_q, d_ff_1_q);
  not not_2 (not_2_out, d_ff_1_q);
  not not_3 (not_3_out, d_ff_2_q);
  and Six (MicroSix, d_ff_3_q, d_ff_2_q, not_2_out);
  and Five (MicroFive, d_ff_3_q, not_3_out, d_ff_1_q);
  not not_4 (not_4_out, d_ff_2_q);
  not not_5 (not_5_out, d_ff_1_q);
  and Four (MicroFour, d_ff_3_q, not_4_out, not_5_out);
  not not_6 (not_6_out, d_ff_3_q);
  not not_7 (not_7_out, d_ff_3_q);
  and Three (MicroThree, not_6_out, d_ff_2_q, d_ff_1_q);
  not not_8 (not_8_out, d_ff_1_q);
  not not_9 (not_9_out, d_ff_3_q);
  not not_10 (not_10_out, d_ff_2_q);
  and Two (MicroTwo, not_7_out, d_ff_2_q, not_8_out);
  and One (MicroOne, not_9_out, not_10_out, d_ff_1_q);
  not not_11 (not_11_out, d_ff_3_q);
  not not_12 (not_12_out, d_ff_2_q);
  not not_13 (not_13_out, d_ff_1_q);
  and Zero (MicroZero, not_11_out, not_12_out, not_13_out);
endmodule
