// Logisim project a6.circ as structural Verilog: 4 circuits, main circuit ALU
module ALU (
  input  L3in,
  input  L2in,
  input  L1in,
  input  L0in,
  input  R3in,
  input  R2in,
  input  R1in,
  input  R0in,
  input  ActiveClock,
  input  IsSubMode,
  output Negative,
  output Zero,
  output Overflow,
  output A3out,
  output A2out,
  output A1out,
  output A0out
);

  wire and_1_out, clock_1_out, controlled_buffer_1_out, controlled_buffer_2_out, controlled_buffer_5_out,
       controlled_buffer_7_out, controlled_buffer_9_out, controlled_buffer_10_out, controlled_buffer_12_out,
       controlled_buffer_14_out, controlled_buffer_15_out, controlled_buffer_16_out,
       controlled_buffer_19_out, controlled_buffer_20_out, fourbitsnegativeb_1_bit1out,
       fourbitsnegativeb_1_bit2out, fourbitsnegativeb_1_bit3out, fourbitsnegativeb_1_bit4out, not_1_out,
       not_2_out, not_3_out, not_4_out, not_5_out, not_6_out, onebitadder_1_carryout, onebitadder_2_carryout,
       onebitadder_3_carryout, onebitadder_4_carryout;

  not not_1 (not_1_out, ActiveClock);
  assign controlled_buffer_1_out = ActiveClock ? L3in : 1'bz;  // Controlled_Buffer controlled_buffer_1
  assign controlled_buffer_2_out = ActiveClock ? L2in : 1'bz;  // Controlled_Buffer controlled_buffer_2
  assign controlled_buffer_1_out = not_1_out ? 1'b0 : 1'bz;  // Controlled_Buffer controlled_buffer_3
  assign controlled_buffer_2_out = not_1_out ? 1'b0 : 1'bz;  // Controlled_Buffer controlled_buffer_4
  OneBitAdder onebitadder_1 (
    .CarryIn(onebitadder_2_carryout), .in1(controlled_buffer_10_out), .in2(controlled_buffer_1_out),
    .Sum(A3out), .CarryOut(onebitadder_1_carryout));
  // NoConnect on onebitadder_1_carryout
  assign controlled_buffer_5_out = ActiveClock ? L1in : 1'bz;  // Controlled_Buffer controlled_buffer_5
  assign controlled_buffer_5_out = not_1_out ? 1'b0 : 1'bz;  // Controlled_Buffer controlled_buffer_6
  assign controlled_buffer_7_out = ActiveClock ? L0in : 1'bz;  // Controlled_Buffer controlled_buffer_7
  assign controlled_buffer_7_out = not_1_out ? 1'b0 : 1'bz;  // Controlled_Buffer controlled_buffer_8
  OneBitAdder onebitadder_2 (
    .CarryIn(onebitadder_3_carryout), .in1(controlled_buffer_14_out), .in2(controlled_buffer_2_out),
    .Sum(A2out), .CarryOut(onebitadder_2_carryout));
  OneBitAdder onebitadder_3 (
    .CarryIn(onebitadder_4_carryout), .in1(controlled_buffer_19_out), .in2(controlled_buffer_5_out),
    .Sum(A1out), .CarryOut(onebitadder_3_carryout));
  OneBitAdder onebitadder_4 (
    .CarryIn(1'b0), .in1(controlled_buffer_20_out), .in2(controlled_buffer_7_out), .Sum(A0out),
    .CarryOut(onebitadder_4_carryout));
  assign controlled_buffer_9_out = not_1_out ? 1'b0 : 1'bz;  // Controlled_Buffer controlled_buffer_9
  assign controlled_buffer_10_out = not_2_out ? controlled_buffer_9_out : 1'bz;  // Controlled_Buffer controlled_buffer_10
  not not_2 (not_2_out, IsSubMode);
  assign controlled_buffer_9_out = ActiveClock ? R3in : 1'bz;  // Controlled_Buffer controlled_buffer_11
  assign controlled_buffer_12_out = ActiveClock ? R2in : 1'bz;  // Controlled_Buffer controlled_buffer_12
  assign controlled_buffer_12_out = not_1_out ? 1'b0 : 1'bz;  // Controlled_Buffer controlled_buffer_13
  assign controlled_buffer_14_out = not_2_out ? controlled_buffer_12_out : 1'bz;  // Controlled_Buffer controlled_buffer_14
  not not_3 (not_3_out, A3out);
  not not_4 (not_4_out, A2out);
  not not_5 (not_5_out, A1out);
  not not_6 (not_6_out, A0out);
  assign controlled_buffer_15_out = ActiveClock ? R0in : 1'bz;  // Controlled_Buffer controlled_buffer_15
  assign controlled_buffer_16_out = ActiveClock ? R1in : 1'bz;  // Controlled_Buffer controlled_buffer_16
  assign controlled_buffer_15_out = not_1_out ? 1'b0 : 1'bz;  // Controlled_Buffer controlled_buffer_17
  assign controlled_buffer_16_out = not_1_out ? 1'b0 : 1'bz;  // Controlled_Buffer controlled_buffer_18
  assign controlled_buffer_19_out = not_2_out ? controlled_buffer_16_out : 1'bz;  // Controlled_Buffer controlled_buffer_19
  assign controlled_buffer_20_out = not_2_out ? controlled_buffer_15_out : 1'bz;  // Controlled_Buffer controlled_buffer_20
  assign controlled_buffer_20_out = IsSubMode ? fourbitsnegativeb_1_bit1out : 1'bz;  // Controlled_Buffer controlled_buffer_21
  Clock clock_1 (.out(clock_1_out));
  and and_1 (and_1_out, not_3_out, not_4_out, not_5_out, not_6_out);
  assign controlled_buffer_14_out = IsSubMode ? fourbitsnegativeb_1_bit3out : 1'bz;  // Controlled_Buffer controlled_buffer_22
  assign controlled_buffer_19_out = IsSubMode ? fourbitsnegativeb_1_bit2out : 1'bz;  // Controlled_Buffer controlled_buffer_23
  and and_2 (Zero, clock_1_out, and_1_out);
  OverFlowDetect overflowdetect_1 (
    .SignBitOfA(controlled_buffer_1_out), .SignBitOfB(controlled_buffer_10_out), .SignBitOfResult(A3out),
    .Overflow(Overflow));
  FourBitsNegativeB fourbitsnegativeb_1 (
    .Bit4In(controlled_buffer_9_out), .Bit3In(controlled_buffer_12_out), .Bit2In(controlled_buffer_16_out),
    .Bit1In(controlled_buffer_15_out), .Bit4Out(fourbitsnegativeb_1_bit4out),
    .Bit3Out(fourbitsnegativeb_1_bit3out), .Bit2Out(fourbitsnegativeb_1_bit2out),
    .Bit1Out(fourbitsnegativeb_1_bit1out));
  assign controlled_buffer_10_out = IsSubMode ? fourbitsnegativeb_1_bit4out : 1'bz;  // Controlled_Buffer controlled_buffer_24

  assign Negative = A3out;

  // Notes on the sheet:
  //   L input
  //   A-out output
  //   R input
endmodule

module OneBitAdder (
  input  CarryIn,
  input  in1,
  input  in2,
  output Sum,
  output CarryOut
);

  wire and_1_out, and_2_out, and_3_out, and_4_out, and_5_out, and_6_out, and_7_out, not_1_out, not_2_out,
       not_3_out;

  not not_1 (not_1_out, in1);
  not not_2 (not_2_out, in2);
  not not_3 (not_3_out, CarryIn);
  and and_1 (and_1_out, in1, not_2_out, not_3_out);
  and and_2 (and_2_out, not_1_out, in2, not_3_out);
  and and_3 (and_3_out, not_1_out, not_2_out, CarryIn);
  and and_4 (and_4_out, in1, in2, CarryIn);
  and and_5 (and_5_out, CarryIn, in1);
  and and_6 (and_6_out, CarryIn, in2);
  and and_7 (and_7_out, in2, in1);
  or or_1 (Sum, and_1_out, and_2_out, and_3_out, and_4_out);
  or or_2 (CarryOut, and_5_out, and_6_out, and_7_out);
endmodule

module FourBitsNegativeB (
  input  Bit4In,
  input  Bit3In,
  input  Bit2In,
  input  Bit1In,
  output Bit4Out,
  output Bit3Out,
  output Bit2Out,
  output Bit1Out
);

  wire not_1_out, not_2_out, not_3_out, not_4_out, onebitadder_1_carryout, onebitadder_2_carryout,
       onebitadder_3_carryout, onebitadder_4_carryout;

  not not_1 (not_1_out, Bit4In);
  OneBitAdder onebitadder_1 (
    .CarryIn(onebitadder_2_carryout), .in1(not_1_out), .in2(1'b0), .Sum(Bit4Out),
    .CarryOut(onebitadder_1_carryout));
  // NoConnect on onebitadder_1_carryout
  not not_2 (not_2_out, Bit3In);
  OneBitAdder onebitadder_2 (
    .CarryIn(onebitadder_3_carryout), .in1(not_2_out), .in2(1'b0), .Sum(Bit3Out),
    .CarryOut(onebitadder_2_carryout));
  not not_3 (not_3_out, Bit2In);
  OneBitAdder onebitadder_3 (
    .CarryIn(onebitadder_4_carryout), .in1(not_3_out), .in2(1'b0), .Sum(Bit2Out),
    .CarryOut(onebitadder_3_carryout));
  not not_4 (not_4_out, Bit1In);
  OneBitAdder onebitadder_4 (
    .CarryIn(1'b0), .in1(not_4_out), .in2(1'b1), .Sum(Bit1Out), .CarryOut(onebitadder_4_carryout));
endmodule

module OverFlowDetect (
  input  SignBitOfA,
  input  SignBitOfB,
  input  SignBitOfResult,
  output Overflow
);

  wire and_1_out, and_2_out, not_1_out, not_2_out, not_3_out;

  not not_1 (not_1_out, SignBitOfA);
  not not_2 (not_2_out, SignBitOfB);
  not not_3 (not_3_out, SignBitOfResult);
  and and_1 (and_1_out, not_1_out, not_2_out, SignBitOfResult);
  and and_2 (and_2_out, SignBitOfA, SignBitOfB, not_3_out);
  or or_1 (Overflow, and_1_out, and_2_out);
endmodule
