// Logisim project project.circ as structural Verilog: 11 circuits, main circuit Main
module Main (
  input  in_1
);

  wire Address0_out, Address1_out, alu_1_a0out, alu_1_a1out, alu_1_a2out, alu_1_a3out, alu_2_a0out,
       alu_2_a1out, alu_2_a2out, alu_2_a3out, alu_2_negative, alu_2_overflow, and_1_out, clock_2_out,
       controlled_buffer_1_out, controlled_buffer_2_out, controlled_buffer_4_out, controlled_buffer_10_out,
       controlled_buffer_11_out, controlled_buffer_12_out, controlled_buffer_13_out,
       controlled_buffer_14_out, controlled_buffer_16_out, controlled_buffer_17_out,
       controlled_buffer_18_out, controlled_buffer_19_out, controlled_buffer_20_out,
       controlled_buffer_21_out, controlled_buffer_22_out, controlled_buffer_23_out,
       controlled_buffer_24_out, controlled_buffer_25_out, controlled_buffer_26_out,
       controlled_buffer_27_out, controlled_buffer_32_out, controlled_buffer_33_out,
       controlled_buffer_34_out, controlled_buffer_35_out, controlled_buffer_36_out,
       controlled_buffer_37_out, controlled_buffer_38_out, controlled_buffer_39_out,
       controlled_buffer_40_out, controlled_buffer_49_out, controlled_buffer_50_out,
       controlled_buffer_51_out, controlled_buffer_52_out, controlled_buffer_58_out,
       controlled_buffer_59_out, controlled_buffer_60_out, controlled_buffer_61_out,
       controlled_buffer_66_out, controlled_buffer_67_out, controlled_buffer_68_out,
       controlled_buffer_69_out, controlled_buffer_70_out, controlled_buffer_71_out,
       controlled_buffer_72_out, DisplayIn_bit0out, DisplayIn_bit1out, DisplayIn_bit2out, DisplayIn_bit3out,
       displayscreenblackbox_1_d1b6, displayscreenblackbox_1_d1b12, displayscreenblackbox_1_d1b0345,
       displayscreenblackbox_1_d2b0, displayscreenblackbox_1_d2b1, displayscreenblackbox_1_d2b2,
       displayscreenblackbox_1_d2b3, displayscreenblackbox_1_d2b4, displayscreenblackbox_1_d2b5,
       displayscreenblackbox_1_d2b6, exe_out, functionofmicrocounter_1_five, functionofmicrocounter_1_four,
       functionofmicrocounter_1_one, functionofmicrocounter_1_seven, functionofmicrocounter_1_six,
       functionofmicrocounter_1_three, functionofmicrocounter_1_two, functionofmicrocounter_1_zero,
       HaltCommand_out, I0000_out, I0000S0_out, I0000S1_out, I0000S2_out, I0000S3_out, I0001_out,
       I0001S0_out, I0001S1_out, I0001S2_out, I0001S3_out, I01X0S2_out, I01X1S2_out, I0010_out, I0010S0_out,
       I0010S1_out, I0010S2_out, I0010S3_out, I010Y_S1_out, I0011_out, I0011S0_out, I0011S1_out, I0011S2_out,
       I0011S3_out, I011YS1_out, I0100_out, I0100S0_out, I0100S1_out, I0100S2_out, I0100S3_out, I0101_out,
       I0101S0_out, I0101S1_out, I0101S2_out, I0101S3_out, I0110_out, I0110S0_out, I0110S1_out, I0110S2_out,
       I0110S3_out, I0111_out, I0111S0_out, I0111S1_out, I0111S2_out, I0111S3_out, I1000_out, I1000S0_out,
       I1000S1_out, I1000S2_out, I1000S3_out, I1010_out, I1010S0_out, I1010S1_out, I1010S2_out, I1010S13_out,
       I1100_out, I1100S0_out, I1100S1_out, I1100S2_out, I1100S3_out, I1110_out, I1110S0_out, I1110S1_out,
       I1110S2_out, I1110S3_out, IR_bit0out, IR_bit1out, IR_bit2out, IR_bit3out, IsHalted_q, L_bit0out,
       L_bit1out, L_bit2out, L_bit3out, MAR_bit0out, MAR_bit1out, MAR_bit2out, MAR_bit3out, MBR_bit0out,
       MBR_bit1out, MBR_bit2out, MBR_bit3out, MicroFive_out, MicroFour_out, MicroSix_out, mode_out,
       not_1_out, not_2_out, not_3_out, not_4_out, not_5_out, not_6_out, not_7_out, not_8_out, not_9_out,
       not_10_out, not_11_out, not_12_out, not_13_out, not_14_out, not_15_out, not_16_out, not_17_out,
       not_18_out, not_19_out, not_20_out, not_21_out, not_22_out, not_23_out, not_24_out, not_25_out,
       not_26_out, not_27_out, not_28_out, not_29_out, not_30_out, not_31_out, not_32_out, not_33_out,
       or_1_out, or_2_out, or_3_out, or_4_out, or_5_out, or_6_out, or_7_out, or_8_out, or_9_out, or_10_out,
       or_11_out, or_12_out, or_13_out, or_14_out, or_15_out, pc_nibble_1_bit0out, pc_nibble_1_bit1out,
       pc_nibble_1_bit2out, pc_nibble_1_bit3out, R0_bit0out, R0_bit1out, R0_bit2out, R0_bit3out, R1_bit0out,
       R1_bit1out, R1_bit2out, R1_bit3out, R_bit0out, R_bit1out, R_bit2out, R_bit3out, RAM_addrzerobit0,
       RAM_addrzerobit1, RAM_addrzerobit2, RAM_addrzerobit3, RAM_dataoutlsb, RAM_dataoutmsb, RAM_out_12,
       RAM_out_13, read_mode_out, Set_Read_mode_out, Set_read_out, Set_write_out, undriven, undriven_2,
       undriven_3, write_mode_out;

  assign controlled_buffer_1_out = Address1_out ? 1'b0 : 1'bz;  // Controlled_Buffer controlled_buffer_1
  assign controlled_buffer_2_out = Address1_out ? 1'b0 : 1'bz;  // Controlled_Buffer controlled_buffer_2
  assign controlled_buffer_2_out = Address0_out ? 1'b0 : 1'bz;  // Controlled_Buffer controlled_buffer_3
  assign controlled_buffer_4_out = Address0_out ? 1'b0 : 1'bz;  // Controlled_Buffer controlled_buffer_4
  assign controlled_buffer_1_out = Address0_out ? 1'b0 : 1'bz;  // Controlled_Buffer controlled_buffer_5
  or Address0 (Address0_out, or_13_out, I01X0S2_out);
  assign controlled_buffer_4_out = Address1_out ? 1'b1 : 1'bz;  // Controlled_Buffer controlled_buffer_6
  or Address1 (Address1_out, or_14_out, I01X1S2_out);
  assign controlled_buffer_1_out = MicroFive_out ? MAR_bit2out : 1'bz;  // Controlled_Buffer controlled_buffer_7
  assign controlled_buffer_2_out = MicroFive_out ? MAR_bit1out : 1'bz;  // Controlled_Buffer controlled_buffer_8
  assign controlled_buffer_4_out = MicroFive_out ? MAR_bit0out : 1'bz;  // Controlled_Buffer controlled_buffer_9
  or exe (exe_out, write_mode_out, read_mode_out);
  or mode (mode_out, Set_write_out, Set_read_out);
  or or_1 (or_1_out, I01X0S2_out, I01X1S2_out);
  assign controlled_buffer_10_out = or_1_out ? controlled_buffer_16_out : 1'bz;  // Controlled_Buffer controlled_buffer_10
  assign controlled_buffer_11_out = or_1_out ? controlled_buffer_17_out : 1'bz;  // Controlled_Buffer controlled_buffer_11
  assign controlled_buffer_12_out = or_1_out ? controlled_buffer_18_out : 1'bz;  // Controlled_Buffer controlled_buffer_12
  assign controlled_buffer_13_out = or_1_out ? controlled_buffer_19_out : 1'bz;  // Controlled_Buffer controlled_buffer_13
  or Set_read (Set_read_out, Set_Read_mode_out, MicroFour_out);
  assign controlled_buffer_14_out = Set_read_out ? 1'b1 : 1'bz;  // Controlled_Buffer controlled_buffer_14
  assign controlled_buffer_14_out = Set_write_out ? 1'b0 : 1'bz;  // Controlled_Buffer controlled_buffer_15
  buf Set_write (Set_write_out, or_15_out);  // OR_Gate
  or read_mode (read_mode_out, or_13_out, MicroFive_out, or_14_out);
  or write_mode (write_mode_out, I01X0S2_out, I01X1S2_out);
  assign controlled_buffer_16_out = or_2_out ? RAM_dataoutmsb : 1'bz;  // Controlled_Buffer controlled_buffer_16
  RAM1 RAM (
    .RamClock(exe_out), .ModeClock(mode_out), .AddrBit2(controlled_buffer_1_out),
    .AddrBit1(controlled_buffer_2_out), .AddrLSB(controlled_buffer_4_out), .Mode(controlled_buffer_14_out),
    .DataInMSB(controlled_buffer_10_out), .DataInBit2(controlled_buffer_11_out),
    .DataInBit1(controlled_buffer_12_out), .DataInLSB(controlled_buffer_13_out), .DataOutMSB(RAM_dataoutmsb),
    .out_12(RAM_out_12), .out_13(RAM_out_13), .DataOutLSB(RAM_dataoutlsb), .AddrZeroBit0(RAM_addrzerobit0),
    .AddrZeroBit1(RAM_addrzerobit1), .AddrZeroBit2(RAM_addrzerobit2), .AddrZeroBit3(RAM_addrzerobit3));
  assign controlled_buffer_17_out = or_2_out ? RAM_out_12 : 1'bz;  // Controlled_Buffer controlled_buffer_17
  assign controlled_buffer_18_out = or_2_out ? RAM_out_13 : 1'bz;  // Controlled_Buffer controlled_buffer_18
  assign controlled_buffer_19_out = or_2_out ? RAM_dataoutlsb : 1'bz;  // Controlled_Buffer controlled_buffer_19
  or or_2 (or_2_out, or_14_out, MicroFive_out, or_13_out);
  Clock clock_1 ();  // open: out
  Nibble DisplayIn (
    .Bit3In(RAM_addrzerobit3), .Bit2In(RAM_addrzerobit2), .Bit1In(RAM_addrzerobit1),
    .Bit0In(RAM_addrzerobit0), .Set(1'b1), .Bit3Out(DisplayIn_bit3out), .Bit2Out(DisplayIn_bit2out),
    .Bit1Out(DisplayIn_bit1out), .Bit0Out(DisplayIn_bit0out));
  // NoConnect on undriven
  assign controlled_buffer_20_out = or_3_out ? controlled_buffer_16_out : 1'bz;  // Controlled_Buffer controlled_buffer_20
  assign controlled_buffer_21_out = or_3_out ? controlled_buffer_17_out : 1'bz;  // Controlled_Buffer controlled_buffer_21
  assign controlled_buffer_22_out = or_3_out ? controlled_buffer_18_out : 1'bz;  // Controlled_Buffer controlled_buffer_22
  assign controlled_buffer_23_out = or_3_out ? controlled_buffer_19_out : 1'bz;  // Controlled_Buffer controlled_buffer_23
  or or_3 (or_3_out, or_14_out, I010Y_S1_out, MicroFive_out, I011YS1_out, or_13_out);
  // NoConnect on MAR_bit3out
  Nibble MAR (
    .Bit3In(undriven), .Bit2In(pc_nibble_1_bit2out), .Bit1In(pc_nibble_1_bit1out),
    .Bit0In(pc_nibble_1_bit0out), .Set(1'b1), .Bit3Out(MAR_bit3out), .Bit2Out(MAR_bit2out),
    .Bit1Out(MAR_bit1out), .Bit0Out(MAR_bit0out));
  Nibble MBR (
    .Bit3In(controlled_buffer_20_out), .Bit2In(controlled_buffer_21_out), .Bit1In(controlled_buffer_22_out),
    .Bit0In(controlled_buffer_23_out), .Set(or_3_out), .Bit3Out(MBR_bit3out), .Bit2Out(MBR_bit2out),
    .Bit1Out(MBR_bit1out), .Bit0Out(MBR_bit0out));
  DisplayScreenBlackbox displayscreenblackbox_1 (
    .MSBBit(DisplayIn_bit3out), .Bit2(DisplayIn_bit2out), .Bit1(DisplayIn_bit1out),
    .LSBBit(DisplayIn_bit0out), .D1B0345(displayscreenblackbox_1_d1b0345),
    .D1B12(displayscreenblackbox_1_d1b12), .D1B6(displayscreenblackbox_1_d1b6),
    .D2B0(displayscreenblackbox_1_d2b0), .D2B1(displayscreenblackbox_1_d2b1),
    .D2B2(displayscreenblackbox_1_d2b2), .D2B3(displayscreenblackbox_1_d2b3),
    .D2B4(displayscreenblackbox_1_d2b4), .D2B5(displayscreenblackbox_1_d2b5),
    .D2B6(displayscreenblackbox_1_d2b6));
  _7_Segment_Display u_7_segment_display_1 (
    .g(displayscreenblackbox_1_d1b6), .f(displayscreenblackbox_1_d1b0345),
    .a(displayscreenblackbox_1_d1b0345), .b(displayscreenblackbox_1_d1b12),
    .e(displayscreenblackbox_1_d1b0345), .d(displayscreenblackbox_1_d1b0345),
    .c(displayscreenblackbox_1_d1b12));  // open: dp
  assign controlled_buffer_24_out = MicroFive_out ? MBR_bit1out : 1'bz;  // Controlled_Buffer controlled_buffer_24
  assign controlled_buffer_25_out = MicroFive_out ? MBR_bit2out : 1'bz;  // Controlled_Buffer controlled_buffer_25
  assign controlled_buffer_26_out = MicroFive_out ? MBR_bit3out : 1'bz;  // Controlled_Buffer controlled_buffer_26
  assign controlled_buffer_27_out = MicroFive_out ? MBR_bit0out : 1'bz;  // Controlled_Buffer controlled_buffer_27
  assign controlled_buffer_16_out = or_4_out ? MBR_bit3out : 1'bz;  // Controlled_Buffer controlled_buffer_28
  assign controlled_buffer_17_out = or_4_out ? MBR_bit2out : 1'bz;  // Controlled_Buffer controlled_buffer_29
  assign controlled_buffer_18_out = or_4_out ? MBR_bit1out : 1'bz;  // Controlled_Buffer controlled_buffer_30
  assign controlled_buffer_19_out = or_4_out ? MBR_bit0out : 1'bz;  // Controlled_Buffer controlled_buffer_31
  or or_4 (or_4_out, I01X1S2_out, I0010S2_out, I0001S2_out, I0011S2_out, I0000S2_out, I01X0S2_out);
  _7_Segment_Display u_7_segment_display_2 (
    .g(displayscreenblackbox_1_d2b6), .f(displayscreenblackbox_1_d2b5), .a(displayscreenblackbox_1_d2b0),
    .b(displayscreenblackbox_1_d2b1), .e(displayscreenblackbox_1_d2b4), .d(displayscreenblackbox_1_d2b3),
    .c(displayscreenblackbox_1_d2b2));  // open: dp
  or or_5 (or_5_out, I0001S2_out, I0000S2_out);
  or or_6 (or_6_out, I0011S2_out, I0010S2_out);
  assign controlled_buffer_32_out = or_5_out ? controlled_buffer_16_out : 1'bz;  // Controlled_Buffer controlled_buffer_32
  assign controlled_buffer_33_out = or_5_out ? controlled_buffer_17_out : 1'bz;  // Controlled_Buffer controlled_buffer_33
  assign controlled_buffer_34_out = or_5_out ? controlled_buffer_18_out : 1'bz;  // Controlled_Buffer controlled_buffer_34
  assign controlled_buffer_35_out = or_5_out ? controlled_buffer_19_out : 1'bz;  // Controlled_Buffer controlled_buffer_35
  assign controlled_buffer_36_out = or_5_out ? or_5_out : 1'bz;  // Controlled_Buffer controlled_buffer_36
  assign controlled_buffer_37_out = or_6_out ? controlled_buffer_16_out : 1'bz;  // Controlled_Buffer controlled_buffer_37
  assign controlled_buffer_38_out = or_6_out ? controlled_buffer_17_out : 1'bz;  // Controlled_Buffer controlled_buffer_38
  assign controlled_buffer_39_out = or_6_out ? controlled_buffer_18_out : 1'bz;  // Controlled_Buffer controlled_buffer_39
  assign controlled_buffer_40_out = or_6_out ? controlled_buffer_19_out : 1'bz;  // Controlled_Buffer controlled_buffer_40
  assign controlled_buffer_16_out = I010Y_S1_out ? R0_bit3out : 1'bz;  // Controlled_Buffer controlled_buffer_41
  assign controlled_buffer_17_out = I010Y_S1_out ? R0_bit2out : 1'bz;  // Controlled_Buffer controlled_buffer_42
  assign controlled_buffer_18_out = I010Y_S1_out ? R0_bit1out : 1'bz;  // Controlled_Buffer controlled_buffer_43
  Nibble R1 (
    .Bit3In(controlled_buffer_37_out), .Bit2In(controlled_buffer_38_out), .Bit1In(controlled_buffer_39_out),
    .Bit0In(controlled_buffer_40_out), .Set(or_6_out), .Bit3Out(R1_bit3out), .Bit2Out(R1_bit2out),
    .Bit1Out(R1_bit1out), .Bit0Out(R1_bit0out));
  Nibble R0 (
    .Bit3In(controlled_buffer_32_out), .Bit2In(controlled_buffer_33_out), .Bit1In(controlled_buffer_34_out),
    .Bit0In(controlled_buffer_35_out), .Set(controlled_buffer_36_out), .Bit3Out(R0_bit3out),
    .Bit2Out(R0_bit2out), .Bit1Out(R0_bit1out), .Bit0Out(R0_bit0out));
  assign controlled_buffer_19_out = I010Y_S1_out ? R0_bit0out : 1'bz;  // Controlled_Buffer controlled_buffer_44
  assign controlled_buffer_16_out = I011YS1_out ? R1_bit3out : 1'bz;  // Controlled_Buffer controlled_buffer_45
  assign controlled_buffer_17_out = I011YS1_out ? R1_bit2out : 1'bz;  // Controlled_Buffer controlled_buffer_46
  assign controlled_buffer_18_out = I011YS1_out ? R1_bit1out : 1'bz;  // Controlled_Buffer controlled_buffer_47
  assign controlled_buffer_19_out = I011YS1_out ? R1_bit0out : 1'bz;  // Controlled_Buffer controlled_buffer_48
  and I1000S0 (I1000S0_out, functionofmicrocounter_1_zero, I1000_out);
  assign controlled_buffer_49_out = or_9_out ? R0_bit3out : 1'bz;  // Controlled_Buffer controlled_buffer_49
  assign controlled_buffer_50_out = or_9_out ? R0_bit2out : 1'bz;  // Controlled_Buffer controlled_buffer_50
  assign controlled_buffer_51_out = or_9_out ? R0_bit1out : 1'bz;  // Controlled_Buffer controlled_buffer_51
  assign controlled_buffer_52_out = or_9_out ? R0_bit0out : 1'bz;  // Controlled_Buffer controlled_buffer_52
  assign controlled_buffer_36_out = or_7_out ? or_7_out : 1'bz;  // Controlled_Buffer controlled_buffer_53
  or or_7 (or_7_out, I1000S1_out, I1100S1_out, I1010S1_out, I1110S1_out);
  assign controlled_buffer_32_out = or_7_out ? alu_1_a3out : 1'bz;  // Controlled_Buffer controlled_buffer_54
  assign controlled_buffer_33_out = or_7_out ? alu_1_a2out : 1'bz;  // Controlled_Buffer controlled_buffer_55
  assign controlled_buffer_34_out = or_7_out ? alu_1_a1out : 1'bz;  // Controlled_Buffer controlled_buffer_56
  assign controlled_buffer_35_out = or_7_out ? alu_1_a0out : 1'bz;  // Controlled_Buffer controlled_buffer_57
  and I1000S1 (I1000S1_out, functionofmicrocounter_1_one, I1000_out);
  and I1000S2 (I1000S2_out, functionofmicrocounter_1_two, I1000_out);
  and I1000S3 (I1000S3_out, functionofmicrocounter_1_three, I1000_out);
  // NoConnect on I1000S2_out
  // NoConnect on I1000S3_out
  and I1010S0 (I1010S0_out, functionofmicrocounter_1_zero, I1010_out);
  and I1010S1 (I1010S1_out, functionofmicrocounter_1_one, I1010_out);
  or or_8 (or_8_out, I1010S0_out, I1110S0_out);
  or or_9 (or_9_out, or_10_out, or_8_out);
  assign controlled_buffer_58_out = or_10_out ? controlled_buffer_52_out : 1'bz;  // Controlled_Buffer controlled_buffer_58
  and I1010S2 (I1010S2_out, functionofmicrocounter_1_two, I1010_out);
  and I1010S13 (I1010S13_out, functionofmicrocounter_1_three, I1010_out);
  and I1100S0 (I1100S0_out, functionofmicrocounter_1_zero, I1100_out);
  // NoConnect on I1010S2_out
  // NoConnect on I1010S13_out
  or or_10 (or_10_out, I1000S0_out, I1100S0_out);
  assign controlled_buffer_59_out = or_10_out ? controlled_buffer_49_out : 1'bz;  // Controlled_Buffer controlled_buffer_59
  assign controlled_buffer_60_out = or_10_out ? controlled_buffer_50_out : 1'bz;  // Controlled_Buffer controlled_buffer_60
  assign controlled_buffer_61_out = or_10_out ? controlled_buffer_51_out : 1'bz;  // Controlled_Buffer controlled_buffer_61
  and I1100S1 (I1100S1_out, functionofmicrocounter_1_one, I1100_out);
  and I1100S2 (I1100S2_out, functionofmicrocounter_1_two, I1100_out);
  and I1100S3 (I1100S3_out, functionofmicrocounter_1_three, I1100_out);
  // NoConnect on I1100S2_out
  // NoConnect on I1100S3_out
  Nibble L (
    .Bit3In(controlled_buffer_49_out), .Bit2In(controlled_buffer_50_out), .Bit1In(controlled_buffer_51_out),
    .Bit0In(controlled_buffer_52_out), .Set(or_9_out), .Bit3Out(L_bit3out), .Bit2Out(L_bit2out),
    .Bit1Out(L_bit1out), .Bit0Out(L_bit0out));
  and I1110S0 (I1110S0_out, functionofmicrocounter_1_zero, I1110_out);
  and I1110S1 (I1110S1_out, functionofmicrocounter_1_one, I1110_out);
  assign controlled_buffer_58_out = or_8_out ? R1_bit0out : 1'bz;  // Controlled_Buffer controlled_buffer_62
  and I1110S2 (I1110S2_out, functionofmicrocounter_1_two, I1110_out);
  and I1110S3 (I1110S3_out, functionofmicrocounter_1_three, I1110_out);
  // NoConnect on I1110S2_out
  // NoConnect on I1110S3_out
  assign controlled_buffer_59_out = or_8_out ? R1_bit3out : 1'bz;  // Controlled_Buffer controlled_buffer_63
  assign controlled_buffer_60_out = or_8_out ? R1_bit2out : 1'bz;  // Controlled_Buffer controlled_buffer_64
  assign controlled_buffer_61_out = or_8_out ? R1_bit1out : 1'bz;  // Controlled_Buffer controlled_buffer_65
  ALU alu_1 (
    .L3in(L_bit3out), .L2in(L_bit2out), .L1in(L_bit1out), .L0in(L_bit0out), .R3in(R_bit3out),
    .R2in(R_bit2out), .R1in(R_bit1out), .R0in(R_bit0out), .ActiveClock(or_7_out), .IsSubMode(or_12_out),
    .A3out(alu_1_a3out), .A2out(alu_1_a2out), .A1out(alu_1_a1out), .A0out(alu_1_a0out));  // open: Negative, Zero, Overflow
  assign controlled_buffer_66_out = MicroFive_out ? controlled_buffer_26_out : 1'bz;  // Controlled_Buffer controlled_buffer_66
  assign controlled_buffer_67_out = MicroFive_out ? controlled_buffer_25_out : 1'bz;  // Controlled_Buffer controlled_buffer_67
  assign controlled_buffer_68_out = MicroFive_out ? controlled_buffer_24_out : 1'bz;  // Controlled_Buffer controlled_buffer_68
  assign controlled_buffer_69_out = MicroFive_out ? controlled_buffer_27_out : 1'bz;  // Controlled_Buffer controlled_buffer_69
  Nibble IR (
    .Bit3In(controlled_buffer_66_out), .Bit2In(controlled_buffer_67_out), .Bit1In(controlled_buffer_68_out),
    .Bit0In(controlled_buffer_69_out), .Set(MicroFive_out), .Bit3Out(IR_bit3out), .Bit2Out(IR_bit2out),
    .Bit1Out(IR_bit1out), .Bit0Out(IR_bit0out));
  Nibble R (
    .Bit3In(controlled_buffer_59_out), .Bit2In(controlled_buffer_60_out), .Bit1In(controlled_buffer_61_out),
    .Bit0In(controlled_buffer_58_out), .Set(or_9_out), .Bit3Out(R_bit3out), .Bit2Out(R_bit2out),
    .Bit1Out(R_bit1out), .Bit0Out(R_bit0out));
  and HaltCommand (HaltCommand_out, IR_bit3out, IR_bit2out, IR_bit1out, IR_bit0out, and_1_out);
  D_Flip_Flop #(.trigger("high")) IsHalted (
    .D(HaltCommand_out), .clk(HaltCommand_out), .Q(IsHalted_q));  // open: Qn, preset, reset
  not not_1 (not_1_out, IR_bit2out);
  and I1000 (I1000_out, and_1_out, IR_bit3out, not_1_out, not_2_out, not_3_out);
  not not_2 (not_2_out, IR_bit1out);
  not not_3 (not_3_out, IR_bit0out);
  not not_4 (not_4_out, IR_bit2out);
  and I1010 (I1010_out, and_1_out, IR_bit3out, not_4_out, IR_bit1out, not_5_out);
  not not_5 (not_5_out, IR_bit0out);
  and I1100 (I1100_out, and_1_out, IR_bit3out, IR_bit2out, not_6_out, not_7_out);
  not not_6 (not_6_out, IR_bit1out);
  not not_7 (not_7_out, IR_bit0out);
  and I1110 (I1110_out, and_1_out, IR_bit3out, IR_bit2out, IR_bit1out, not_8_out);
  not not_8 (not_8_out, IR_bit0out);
  and and_1 (and_1_out, not_9_out, clock_2_out);
  not not_9 (not_9_out, IsHalted_q);
  Clock clock_2 (.out(clock_2_out));
  or or_11 (or_11_out, and_1_out, in_1);
  // NoConnect on undriven_2
  or or_12 (or_12_out, I1100_out, I1110_out);
  and MicroSix (MicroSix_out, functionofmicrocounter_1_six, and_1_out);
  FunctionOfMicroCounter functionofmicrocounter_1 (
    .CounterClock(or_11_out), .ResetToFour(in_1), .Zero(functionofmicrocounter_1_zero),
    .One(functionofmicrocounter_1_one), .Two(functionofmicrocounter_1_two),
    .Three(functionofmicrocounter_1_three), .Four(functionofmicrocounter_1_four),
    .Five(functionofmicrocounter_1_five), .Six(functionofmicrocounter_1_six),
    .Seven(functionofmicrocounter_1_seven));
  and MicroFour (MicroFour_out, functionofmicrocounter_1_four, and_1_out);
  // NoConnect on pc_nibble_1_bit3out
  PC_nibble pc_nibble_1 (
    .Bit3In(undriven_2), .Bit2In(alu_2_a2out), .Bit1In(alu_2_a1out), .Bit0In(alu_2_a0out),
    .Set(MicroSix_out), .Bit3Out(pc_nibble_1_bit3out), .Bit2Out(pc_nibble_1_bit2out),
    .Bit1Out(pc_nibble_1_bit1out), .Bit0Out(pc_nibble_1_bit0out));
  and MicroFive (MicroFive_out, and_1_out, functionofmicrocounter_1_five);
  assign controlled_buffer_70_out = MicroSix_out ? pc_nibble_1_bit2out : 1'bz;  // Controlled_Buffer controlled_buffer_70
  assign controlled_buffer_71_out = MicroSix_out ? pc_nibble_1_bit1out : 1'bz;  // Controlled_Buffer controlled_buffer_71
  assign controlled_buffer_72_out = MicroSix_out ? pc_nibble_1_bit0out : 1'bz;  // Controlled_Buffer controlled_buffer_72
  not not_10 (not_10_out, IR_bit3out);
  not not_11 (not_11_out, IR_bit2out);
  not not_12 (not_12_out, IR_bit1out);
  not not_13 (not_13_out, IR_bit0out);
  not not_14 (not_14_out, IR_bit3out);
  not not_15 (not_15_out, IR_bit2out);
  not not_16 (not_16_out, IR_bit1out);
  not not_17 (not_17_out, IR_bit3out);
  not not_18 (not_18_out, IR_bit2out);
  not not_19 (not_19_out, IR_bit0out);
  not not_20 (not_20_out, IR_bit3out);
  not not_21 (not_21_out, IR_bit2out);
  not not_22 (not_22_out, IR_bit3out);
  not not_23 (not_23_out, IR_bit1out);
  not not_24 (not_24_out, IR_bit0out);
  not not_25 (not_25_out, IR_bit3out);
  not not_26 (not_26_out, IR_bit1out);
  not not_27 (not_27_out, IR_bit3out);
  not not_28 (not_28_out, IR_bit0out);
  not not_29 (not_29_out, IR_bit3out);
  // NoConnect on undriven_3
  not not_30 (not_30_out, 1'b1);
  not not_31 (not_31_out, 1'b1);
  not not_32 (not_32_out, 1'b1);
  not not_33 (not_33_out, 1'b1);
  and I0000 (I0000_out, and_1_out, not_10_out, not_11_out, not_12_out, not_13_out);
  and I0001 (I0001_out, and_1_out, not_14_out, not_15_out, not_16_out, IR_bit0out);
  and I0010 (I0010_out, and_1_out, not_17_out, not_18_out, IR_bit1out, not_19_out);
  and I0011 (I0011_out, and_1_out, not_20_out, not_21_out, IR_bit1out, IR_bit0out);
  and I0100 (I0100_out, and_1_out, not_22_out, IR_bit2out, not_23_out, not_24_out);
  and I0101 (I0101_out, and_1_out, not_25_out, IR_bit2out, not_26_out, IR_bit0out);
  and I0110 (I0110_out, and_1_out, not_27_out, IR_bit2out, IR_bit1out, not_28_out);
  and I0111 (I0111_out, and_1_out, not_29_out, IR_bit2out, IR_bit1out, IR_bit0out);
  and I0000S0 (I0000S0_out, functionofmicrocounter_1_zero, I0000_out);
  and I0000S1 (I0000S1_out, functionofmicrocounter_1_one, I0000_out);
  and I0100S0 (I0100S0_out, functionofmicrocounter_1_zero, I0100_out);
  and I0100S1 (I0100S1_out, functionofmicrocounter_1_one, I0100_out);
  and I0000S2 (I0000S2_out, functionofmicrocounter_1_two, I0000_out);
  and I0000S3 (I0000S3_out, functionofmicrocounter_1_three, I0000_out);
  // NoConnect on I0000S3_out
  or or_13 (or_13_out, I0000S1_out, I0010S1_out);
  and I0100S2 (I0100S2_out, functionofmicrocounter_1_two, I0100_out);
  and I0100S3 (I0100S3_out, functionofmicrocounter_1_three, I0100_out);
  // NoConnect on I0100S3_out
  or I010Y_S1 (I010Y_S1_out, I0100S1_out, I0101S1_out);
  // NoConnect on alu_2_negative
  ALU alu_2 (
    .L3in(undriven_3), .L2in(controlled_buffer_70_out), .L1in(controlled_buffer_71_out),
    .L0in(controlled_buffer_72_out), .R3in(not_30_out), .R2in(not_31_out), .R1in(not_32_out), .R0in(1'b1),
    .ActiveClock(MicroSix_out), .IsSubMode(not_33_out), .Negative(alu_2_negative), .Overflow(alu_2_overflow),
    .A3out(alu_2_a3out), .A2out(alu_2_a2out), .A1out(alu_2_a1out), .A0out(alu_2_a0out));  // open: Zero
  // NoConnect on alu_2_overflow
  // NoConnect on alu_2_a3out
  and I0001S0 (I0001S0_out, functionofmicrocounter_1_zero, I0001_out);
  and I0001S1 (I0001S1_out, functionofmicrocounter_1_one, I0001_out);
  and I0001S2 (I0001S2_out, functionofmicrocounter_1_two, I0001_out);
  or or_14 (or_14_out, I0001S1_out, I0011S1_out);
  and I0101S0 (I0101S0_out, functionofmicrocounter_1_zero, I0101_out);
  and I0101S1 (I0101S1_out, functionofmicrocounter_1_one, I0101_out);
  and I0101S2 (I0101S2_out, functionofmicrocounter_1_two, I0101_out);
  or I01X0S2 (I01X0S2_out, I0100S2_out, I0110S2_out);
  and I0001S3 (I0001S3_out, functionofmicrocounter_1_three, I0001_out);
  and I0010S0 (I0010S0_out, functionofmicrocounter_1_zero, I0010_out);
  and I0010S1 (I0010S1_out, functionofmicrocounter_1_one, I0010_out);
  // NoConnect on I0001S3_out
  and I0101S3 (I0101S3_out, functionofmicrocounter_1_three, I0101_out);
  and I0110S0 (I0110S0_out, functionofmicrocounter_1_zero, I0110_out);
  and I0110S1 (I0110S1_out, functionofmicrocounter_1_one, I0110_out);
  // NoConnect on I0101S3_out
  and I0010S2 (I0010S2_out, functionofmicrocounter_1_two, I0010_out);
  and I0010S3 (I0010S3_out, functionofmicrocounter_1_three, I0010_out);
  // NoConnect on I0010S3_out
  and I0110S2 (I0110S2_out, functionofmicrocounter_1_two, I0110_out);
  and I0110S3 (I0110S3_out, functionofmicrocounter_1_three, I0110_out);
  // NoConnect on I0110S3_out
  or I011YS1 (I011YS1_out, I0110S1_out, I0111S1_out);
  Clock clock_3 ();  // open: out
  and I0011S0 (I0011S0_out, functionofmicrocounter_1_zero, I0011_out);
  and I0011S1 (I0011S1_out, functionofmicrocounter_1_one, I0011_out);
  and I0011S2 (I0011S2_out, functionofmicrocounter_1_two, I0011_out);
  and I0111S0 (I0111S0_out, functionofmicrocounter_1_zero, I0111_out);
  and I0111S1 (I0111S1_out, functionofmicrocounter_1_one, I0111_out);
  and I0111S2 (I0111S2_out, functionofmicrocounter_1_two, I0111_out);
  or I01X1S2 (I01X1S2_out, I0101S2_out, I0111S2_out);
  and I0011S3 (I0011S3_out, functionofmicrocounter_1_three, I0011_out);
  // NoConnect on I0011S3_out
  and I0111S3 (I0111S3_out, functionofmicrocounter_1_three, I0111_out);
  // NoConnect on I0111S3_out
  or Set_Read_mode (Set_Read_mode_out, I0000S0_out, I0001S0_out, I0010S0_out, I0011S0_out);
  or or_15 (or_15_out, I0111S0_out, I0110S0_out, I0101S0_out, I0100S0_out);

  // Notes on the sheet:
  //   Maitree Hirunteeyakul (261122154)
  //   Huy Trinh (261015197)
  //   If IsHalted == 1: The system should NOT perform any task.
  //   Use this line as a CLOCK
  //   Load CU
  //   Save CU
endmodule

module Nibble (
  input  Bit3In,
  input  Bit2In,
  input  Bit1In,
  input  Bit0In,
  input  Set,
  output Bit3Out,
  output Bit2Out,
  output Bit1Out,
  output Bit0Out
);

  D_Flip_Flop #(.trigger("high")) d_ff_1 (.D(Bit3In), .clk(Set), .Q(Bit3Out));  // open: Qn, preset, reset
  D_Flip_Flop #(.trigger("high")) d_ff_2 (.D(Bit2In), .clk(Set), .Q(Bit2Out));  // open: Qn, preset, reset
  D_Flip_Flop #(.trigger("high")) d_ff_3 (.D(Bit1In), .clk(Set), .Q(Bit1Out));  // open: Qn, preset, reset
  D_Flip_Flop #(.trigger("high")) d_ff_4 (.D(Bit0In), .clk(Set), .Q(Bit0Out));  // open: Qn, preset, reset
endmodule

module RAM1 (
  input  RamClock,
  input  ModeClock,
  input  AddrBit2,
  input  AddrBit1,
  input  AddrLSB,
  input  Mode,
  input  DataInMSB,
  input  DataInBit2,
  input  DataInBit1,
  input  DataInLSB,
  output DataOutMSB,
  output out_12,
  output out_13,
  output DataOutLSB,
  output AddrZeroBit0,
  output AddrZeroBit1,
  output AddrZeroBit2,
  output AddrZeroBit3
);

  wire and_1_out, and_2_out, and_3_out, and_4_out, and_5_out, and_6_out, and_7_out, and_8_out, and_9_out,
       and_10_out, and_11_out, and_12_out, and_13_out, and_14_out, and_15_out, and_16_out, and_17_out,
       and_18_out, and_19_out, and_20_out, and_21_out, and_22_out, and_23_out, and_24_out, and_25_out,
       and_26_out, and_27_out, and_28_out, and_29_out, and_30_out, and_31_out, and_32_out, and_33_out,
       and_34_out, and_35_out, and_36_out, and_37_out, and_38_out, and_39_out, and_40_out, and_41_out,
       and_42_out, and_43_out, and_44_out, and_45_out, and_46_out, and_47_out, and_48_out, and_49_out,
       and_50_out, and_51_out, and_52_out, and_53_out, and_54_out, and_55_out, and_56_out, and_57_out,
       and_58_out, and_59_out, and_60_out, and_61_out, and_62_out, and_63_out, and_64_out, and_65_out,
       and_66_out, and_67_out, and_68_out, and_69_out, and_70_out, and_71_out, and_72_out, and_73_out,
       and_74_out, and_75_out, and_76_out, and_77_out, and_78_out, and_79_out, and_80_out, d_ff_1_q,
       d_ff_2_q, d_ff_3_q, d_ff_4_q, d_ff_5_q, d_ff_6_q, d_ff_7_q, d_ff_8_q, d_ff_9_q, d_ff_10_q, d_ff_11_q,
       d_ff_13_q, d_ff_14_q, d_ff_16_q, d_ff_17_q, d_ff_18_q, d_ff_19_q, d_ff_20_q, d_ff_21_q, d_ff_22_q,
       d_ff_24_q, d_ff_26_q, d_ff_29_q, d_ff_30_q, d_ff_31_q, d_ff_32_q, d_ff_33_q, d_ff_34_q, d_ff_35_q,
       d_ff_37_q, d_ff_38_q, d_ff_39_q, d_ff_40_q, d_ff_41_q, d_ff_42_q, d_ff_43_q, not_1_out, not_2_out,
       not_3_out, not_4_out, not_5_out, not_6_out, not_7_out, not_8_out, not_9_out, not_10_out, not_11_out,
       not_12_out, not_13_out, or_1_out, or_2_out, or_3_out, or_4_out;

  D_Flip_Flop #(.trigger("high")) d_ff_1 (.D(AddrBit2), .clk(RamClock), .Q(d_ff_1_q));  // open: Qn, preset, reset
  D_Flip_Flop #(.trigger("high")) d_ff_2 (.D(AddrBit1), .clk(RamClock), .Q(d_ff_2_q));  // open: Qn, preset, reset
  and and_1 (and_1_out, d_ff_1_q, d_ff_2_q, RamClock, d_ff_3_q);
  and and_2 (and_2_out, d_ff_1_q, d_ff_2_q, RamClock, not_1_out);
  not not_1 (not_1_out, d_ff_3_q);
  not not_2 (not_2_out, d_ff_2_q);
  and and_3 (and_3_out, d_ff_1_q, not_2_out, RamClock, d_ff_3_q);
  not not_3 (not_3_out, d_ff_2_q);
  and and_4 (and_4_out, d_ff_1_q, not_3_out, RamClock, not_4_out);
  not not_4 (not_4_out, d_ff_3_q);
  not not_5 (not_5_out, d_ff_1_q);
  and and_5 (and_5_out, not_5_out, d_ff_2_q, RamClock, d_ff_3_q);
  not not_6 (not_6_out, d_ff_1_q);
  and and_6 (and_6_out, not_6_out, d_ff_2_q, RamClock, not_7_out);
  not not_7 (not_7_out, d_ff_3_q);
  not not_8 (not_8_out, d_ff_1_q);
  not not_9 (not_9_out, d_ff_2_q);
  and and_7 (and_7_out, not_8_out, not_9_out, RamClock, d_ff_3_q);
  not not_10 (not_10_out, d_ff_1_q);
  not not_11 (not_11_out, d_ff_2_q);
  and and_8 (and_8_out, not_10_out, not_11_out, RamClock, not_12_out);
  not not_12 (not_12_out, d_ff_3_q);
  D_Flip_Flop #(.trigger("high")) d_ff_3 (.D(AddrLSB), .clk(RamClock), .Q(d_ff_3_q));  // open: Qn, preset, reset
  and and_9 (and_9_out, and_1_out, not_13_out);
  and and_10 (and_10_out, and_2_out, not_13_out);
  and and_11 (and_11_out, and_3_out, not_13_out);
  and and_12 (and_12_out, and_4_out, not_13_out);
  and and_13 (and_13_out, and_5_out, not_13_out);
  and and_14 (and_14_out, and_6_out, not_13_out);
  and and_15 (and_15_out, and_7_out, not_13_out);
  and and_16 (and_16_out, and_8_out, not_13_out);
  not not_13 (not_13_out, d_ff_4_q);
  D_Flip_Flop #(.trigger("high")) d_ff_4 (.D(Mode), .clk(ModeClock), .Q(d_ff_4_q));  // open: Qn, preset, reset
  and and_17 (and_17_out, and_1_out, not_13_out, d_ff_13_q);
  and and_18 (and_18_out, and_2_out, not_13_out, d_ff_13_q);
  and and_19 (and_19_out, and_3_out, not_13_out, d_ff_13_q);
  and and_20 (and_20_out, and_4_out, not_13_out, d_ff_13_q);
  and and_21 (and_21_out, and_5_out, not_13_out, d_ff_13_q);
  and and_22 (and_22_out, and_6_out, not_13_out, d_ff_13_q);
  and and_23 (and_23_out, and_7_out, not_13_out, d_ff_13_q);
  and and_24 (and_24_out, and_8_out, not_13_out, d_ff_13_q);
  D_Flip_Flop #(.trigger("high")) d_ff_5 (.D(and_17_out), .clk(and_9_out), .Q(d_ff_5_q));  // open: Qn, preset, reset
  D_Flip_Flop #(.trigger("high")) d_ff_6 (.D(and_18_out), .clk(and_10_out), .Q(d_ff_6_q));  // open: Qn, preset, reset
  D_Flip_Flop #(.trigger("high")) d_ff_7 (.D(and_19_out), .clk(and_11_out), .Q(d_ff_7_q));  // open: Qn, preset, reset
  D_Flip_Flop #(.trigger("high")) d_ff_8 (.D(and_20_out), .clk(and_12_out), .Q(d_ff_8_q));  // open: Qn, preset, reset
  D_Flip_Flop #(.trigger("high")) d_ff_9 (.D(and_21_out), .clk(and_13_out), .Q(d_ff_9_q));  // open: Qn, preset, reset
  D_Flip_Flop #(.trigger("high")) d_ff_10 (.D(and_22_out), .clk(and_14_out), .Q(d_ff_10_q));  // open: Qn, preset, reset
  D_Flip_Flop #(.trigger("high")) d_ff_11 (.D(and_23_out), .clk(and_15_out), .Q(d_ff_11_q));  // open: Qn, preset, reset
  D_Flip_Flop #(.trigger("high")) d_ff_12 (
    .D(and_24_out), .clk(and_16_out), .Q(AddrZeroBit3));  // open: Qn, preset, reset
  or or_1 (or_1_out, and_25_out, and_26_out, and_27_out, and_28_out, and_29_out, and_30_out, and_31_out, and_32_out);
  and and_25 (and_25_out, d_ff_5_q, and_1_out, d_ff_4_q);
  and and_26 (and_26_out, d_ff_6_q, and_2_out, d_ff_4_q);
  and and_27 (and_27_out, d_ff_7_q, and_3_out, d_ff_4_q);
  and and_28 (and_28_out, d_ff_8_q, and_4_out, d_ff_4_q);
  and and_29 (and_29_out, d_ff_9_q, and_5_out, d_ff_4_q);
  and and_30 (and_30_out, d_ff_10_q, and_6_out, d_ff_4_q);
  and and_31 (and_31_out, d_ff_11_q, and_7_out, d_ff_4_q);
  and and_32 (and_32_out, AddrZeroBit3, and_8_out, d_ff_4_q);
  D_Flip_Flop #(.trigger("high")) d_ff_13 (.D(DataInMSB), .clk(RamClock), .Q(d_ff_13_q));  // open: Qn, preset, reset
  D_Flip_Flop #(.trigger("high")) d_ff_14 (.D(DataInBit2), .clk(RamClock), .Q(d_ff_14_q));  // open: Qn, preset, reset
  D_Flip_Flop #(.trigger("high")) d_ff_15 (.D(or_1_out), .clk(RamClock), .Q(DataOutMSB));  // open: Qn, preset, reset
  and and_33 (and_33_out, and_1_out, not_13_out, d_ff_14_q);
  D_Flip_Flop #(.trigger("high")) d_ff_16 (.D(and_33_out), .clk(and_9_out), .Q(d_ff_16_q));  // open: Qn, preset, reset
  and and_34 (and_34_out, and_2_out, not_13_out, d_ff_14_q);
  D_Flip_Flop #(.trigger("high")) d_ff_17 (.D(and_34_out), .clk(and_10_out), .Q(d_ff_17_q));  // open: Qn, preset, reset
  and and_35 (and_35_out, and_3_out, not_13_out, d_ff_14_q);
  D_Flip_Flop #(.trigger("high")) d_ff_18 (.D(and_35_out), .clk(and_11_out), .Q(d_ff_18_q));  // open: Qn, preset, reset
  and and_36 (and_36_out, and_4_out, not_13_out, d_ff_14_q);
  D_Flip_Flop #(.trigger("high")) d_ff_19 (.D(and_36_out), .clk(and_12_out), .Q(d_ff_19_q));  // open: Qn, preset, reset
  and and_37 (and_37_out, and_5_out, not_13_out, d_ff_14_q);
  D_Flip_Flop #(.trigger("high")) d_ff_20 (.D(and_37_out), .clk(and_13_out), .Q(d_ff_20_q));  // open: Qn, preset, reset
  and and_38 (and_38_out, and_6_out, not_13_out, d_ff_14_q);
  D_Flip_Flop #(.trigger("high")) d_ff_21 (.D(and_38_out), .clk(and_14_out), .Q(d_ff_21_q));  // open: Qn, preset, reset
  and and_39 (and_39_out, and_7_out, not_13_out, d_ff_14_q);
  D_Flip_Flop #(.trigger("high")) d_ff_22 (.D(and_39_out), .clk(and_15_out), .Q(d_ff_22_q));  // open: Qn, preset, reset
  and and_40 (and_40_out, and_8_out, not_13_out, d_ff_14_q);
  D_Flip_Flop #(.trigger("high")) d_ff_23 (
    .D(and_40_out), .clk(and_16_out), .Q(AddrZeroBit2));  // open: Qn, preset, reset
  D_Flip_Flop #(.trigger("high")) d_ff_24 (.D(DataInBit1), .clk(RamClock), .Q(d_ff_24_q));  // open: Qn, preset, reset
  D_Flip_Flop #(.trigger("high")) d_ff_25 (.D(or_2_out), .clk(RamClock), .Q(out_12));  // open: Qn, preset, reset
  or or_2 (or_2_out, and_41_out, and_42_out, and_43_out, and_44_out, and_45_out, and_46_out, and_47_out, and_48_out);
  and and_41 (and_41_out, d_ff_16_q, and_1_out, d_ff_4_q);
  and and_42 (and_42_out, d_ff_17_q, and_2_out, d_ff_4_q);
  and and_43 (and_43_out, d_ff_18_q, and_3_out, d_ff_4_q);
  and and_44 (and_44_out, d_ff_19_q, and_4_out, d_ff_4_q);
  and and_45 (and_45_out, d_ff_20_q, and_5_out, d_ff_4_q);
  and and_46 (and_46_out, d_ff_21_q, and_6_out, d_ff_4_q);
  and and_47 (and_47_out, d_ff_22_q, and_7_out, d_ff_4_q);
  and and_48 (and_48_out, AddrZeroBit2, and_8_out, d_ff_4_q);
  D_Flip_Flop #(.trigger("high")) d_ff_26 (.D(DataInLSB), .clk(RamClock), .Q(d_ff_26_q));  // open: Qn, preset, reset
  D_Flip_Flop #(.trigger("high")) d_ff_27 (.D(or_3_out), .clk(RamClock), .Q(out_13));  // open: Qn, preset, reset
  D_Flip_Flop #(.trigger("high")) d_ff_28 (.D(or_4_out), .clk(RamClock), .Q(DataOutLSB));  // open: Qn, preset, reset
  and and_49 (and_49_out, and_1_out, not_13_out, d_ff_24_q);
  D_Flip_Flop #(.trigger("high")) d_ff_29 (.D(and_49_out), .clk(and_9_out), .Q(d_ff_29_q));  // open: Qn, preset, reset
  and and_50 (and_50_out, and_2_out, not_13_out, d_ff_24_q);
  D_Flip_Flop #(.trigger("high")) d_ff_30 (.D(and_50_out), .clk(and_10_out), .Q(d_ff_30_q));  // open: Qn, preset, reset
  and and_51 (and_51_out, and_3_out, not_13_out, d_ff_24_q);
  D_Flip_Flop #(.trigger("high")) d_ff_31 (.D(and_51_out), .clk(and_11_out), .Q(d_ff_31_q));  // open: Qn, preset, reset
  and and_52 (and_52_out, and_4_out, not_13_out, d_ff_24_q);
  D_Flip_Flop #(.trigger("high")) d_ff_32 (.D(and_52_out), .clk(and_12_out), .Q(d_ff_32_q));  // open: Qn, preset, reset
  and and_53 (and_53_out, and_5_out, not_13_out, d_ff_24_q);
  D_Flip_Flop #(.trigger("high")) d_ff_33 (.D(and_53_out), .clk(and_13_out), .Q(d_ff_33_q));  // open: Qn, preset, reset
  and and_54 (and_54_out, and_6_out, not_13_out, d_ff_24_q);
  D_Flip_Flop #(.trigger("high")) d_ff_34 (.D(and_54_out), .clk(and_14_out), .Q(d_ff_34_q));  // open: Qn, preset, reset
  and and_55 (and_55_out, and_7_out, not_13_out, d_ff_24_q);
  D_Flip_Flop #(.trigger("high")) d_ff_35 (.D(and_55_out), .clk(and_15_out), .Q(d_ff_35_q));  // open: Qn, preset, reset
  and and_56 (and_56_out, and_8_out, not_13_out, d_ff_24_q);
  D_Flip_Flop #(.trigger("high")) d_ff_36 (
    .D(and_56_out), .clk(and_16_out), .Q(AddrZeroBit1));  // open: Qn, preset, reset
  Clock clock_1 ();  // open: out
  or or_3 (or_3_out, and_57_out, and_58_out, and_59_out, and_60_out, and_61_out, and_62_out, and_63_out, and_64_out);
  and and_57 (and_57_out, d_ff_29_q, and_1_out, d_ff_4_q);
  and and_58 (and_58_out, d_ff_30_q, and_2_out, d_ff_4_q);
  and and_59 (and_59_out, d_ff_31_q, and_3_out, d_ff_4_q);
  and and_60 (and_60_out, d_ff_32_q, and_4_out, d_ff_4_q);
  and and_61 (and_61_out, d_ff_33_q, and_5_out, d_ff_4_q);
  and and_62 (and_62_out, d_ff_34_q, and_6_out, d_ff_4_q);
  and and_63 (and_63_out, d_ff_35_q, and_7_out, d_ff_4_q);
  and and_64 (and_64_out, AddrZeroBit1, and_8_out, d_ff_4_q);
  and and_65 (and_65_out, and_1_out, not_13_out, d_ff_26_q);
  D_Flip_Flop #(.trigger("high")) d_ff_37 (.D(and_65_out), .clk(and_9_out), .Q(d_ff_37_q));  // open: Qn, preset, reset
  and and_66 (and_66_out, and_2_out, not_13_out, d_ff_26_q);
  D_Flip_Flop #(.trigger("high")) d_ff_38 (.D(and_66_out), .clk(and_10_out), .Q(d_ff_38_q));  // open: Qn, preset, reset
  and and_67 (and_67_out, and_3_out, not_13_out, d_ff_26_q);
  D_Flip_Flop #(.trigger("high")) d_ff_39 (.D(and_67_out), .clk(and_11_out), .Q(d_ff_39_q));  // open: Qn, preset, reset
  and and_68 (and_68_out, and_4_out, not_13_out, d_ff_26_q);
  D_Flip_Flop #(.trigger("high")) d_ff_40 (.D(and_68_out), .clk(and_12_out), .Q(d_ff_40_q));  // open: Qn, preset, reset
  and and_69 (and_69_out, and_5_out, not_13_out, d_ff_26_q);
  D_Flip_Flop #(.trigger("high")) d_ff_41 (.D(and_69_out), .clk(and_13_out), .Q(d_ff_41_q));  // open: Qn, preset, reset
  and and_70 (and_70_out, and_6_out, not_13_out, d_ff_26_q);
  D_Flip_Flop #(.trigger("high")) d_ff_42 (.D(and_70_out), .clk(and_14_out), .Q(d_ff_42_q));  // open: Qn, preset, reset
  and and_71 (and_71_out, and_7_out, not_13_out, d_ff_26_q);
  D_Flip_Flop #(.trigger("high")) d_ff_43 (.D(and_71_out), .clk(and_15_out), .Q(d_ff_43_q));  // open: Qn, preset, reset
  and and_72 (and_72_out, and_8_out, not_13_out, d_ff_26_q);
  D_Flip_Flop #(.trigger("high")) d_ff_44 (
    .D(and_72_out), .clk(and_16_out), .Q(AddrZeroBit0));  // open: Qn, preset, reset
  or or_4 (or_4_out, and_73_out, and_74_out, and_75_out, and_76_out, and_77_out, and_78_out, and_79_out, and_80_out);
  and and_73 (and_73_out, d_ff_37_q, and_1_out, d_ff_4_q);
  and and_74 (and_74_out, d_ff_38_q, and_2_out, d_ff_4_q);
  and and_75 (and_75_out, d_ff_39_q, and_3_out, d_ff_4_q);
  and and_76 (and_76_out, d_ff_40_q, and_4_out, d_ff_4_q);
  and and_77 (and_77_out, d_ff_41_q, and_5_out, d_ff_4_q);
  and and_78 (and_78_out, d_ff_42_q, and_6_out, d_ff_4_q);
  and and_79 (and_79_out, d_ff_43_q, and_7_out, d_ff_4_q);
  and and_80 (and_80_out, AddrZeroBit0, and_8_out, d_ff_4_q);

  // Notes on the sheet:
  //   3-bit address input pins
  //   Mode input pin
  //   Is Read
  //   4-bit data input pins
  //   4-bit data output pins
endmodule

module PC_nibble (
  input  Bit3In,
  input  Bit2In,
  input  Bit1In,
  input  Bit0In,
  input  Set,
  output Bit3Out,
  output Bit2Out,
  output Bit1Out,
  output Bit0Out
);

  D_Flip_Flop #(.trigger("falling")) d_ff_1 (.D(Bit3In), .clk(Set), .Q(Bit3Out));  // open: Qn, preset, reset
  D_Flip_Flop #(.trigger("falling")) d_ff_2 (.D(Bit2In), .clk(Set), .Q(Bit2Out));  // open: Qn, preset, reset
  D_Flip_Flop #(.trigger("falling")) d_ff_3 (.D(Bit1In), .clk(Set), .Q(Bit1Out));  // open: Qn, preset, reset
  D_Flip_Flop #(.trigger("falling")) d_ff_4 (.D(Bit0In), .clk(Set), .Q(Bit0Out));  // open: Qn, preset, reset
endmodule

module FunctionOfMicroCounter (
  input  CounterClock,
  input  ResetToFour,
  output Zero,
  output One,
  output Two,
  output Three,
  output Four,
  output Five,
  output Six,
  output Seven
);

  MicroCounter microcounter_1 (
    .CounterClock(CounterClock), .ResetToZero(ResetToFour), .MicroZero(Four), .MicroOne(Five),
    .MicroTwo(Six), .MicroThree(Seven), .MicroFour(Zero), .MicroFive(One), .MicroSix(Two), .MicroSeven(Three));
endmodule

module OneBitAdder (
  input  CarryIn,
  input  in1,
  input  in2,
  output Sum,
  output CarryOut
);

  wire and_1_out, and_2_out, and_3_out, and_4_out, and_5_out, and_6_out, and_7_out, not_1_out, not_2_out,
       not_3_out;

  not not_1 (not_1_out, in1);
  not not_2 (not_2_out, in2);
  not not_3 (not_3_out, CarryIn);
  and and_1 (and_1_out, in1, not_2_out, not_3_out);
  and and_2 (and_2_out, not_1_out, in2, not_3_out);
  and and_3 (and_3_out, not_1_out, not_2_out, CarryIn);
  and and_4 (and_4_out, in1, in2, CarryIn);
  and and_5 (and_5_out, CarryIn, in1);
  and and_6 (and_6_out, CarryIn, in2);
  and and_7 (and_7_out, in2, in1);
  or or_1 (Sum, and_1_out, and_2_out, and_3_out, and_4_out);
  or or_2 (CarryOut, and_5_out, and_6_out, and_7_out);
endmodule

module OverFlowDetect (
  input  SignBitOfA,
  input  SignBitOfB,
  input  SignBitOfResult,
  output Overflow
);

  wire and_1_out, and_2_out, not_1_out, not_2_out, not_3_out;

  not not_1 (not_1_out, SignBitOfA);
  not not_2 (not_2_out, SignBitOfB);
  not not_3 (not_3_out, SignBitOfResult);
  and and_1 (and_1_out, not_1_out, not_2_out, SignBitOfResult);
  and and_2 (and_2_out, SignBitOfA, SignBitOfB, not_3_out);
  or or_1 (Overflow, and_1_out, and_2_out);
endmodule

module NewFourBitsNegativeB (
  input  Bit4In,
  input  Bit3In,
  input  Bit2In,
  input  Bit1In,
  output Bit4Out,
  output Bit3Out,
  output Bit2Out,
  output Bit1Out
);

  wire not_1_out, not_2_out, not_3_out, not_4_out, onebitadder_1_carryout, onebitadder_2_carryout,
       onebitadder_3_carryout, onebitadder_4_carryout;

  not not_1 (not_1_out, Bit4In);
  OneBitAdder onebitadder_1 (
    .CarryIn(onebitadder_2_carryout), .in1(not_1_out), .in2(1'b0), .Sum(Bit4Out),
    .CarryOut(onebitadder_1_carryout));
  // NoConnect on onebitadder_1_carryout
  not not_2 (not_2_out, Bit3In);
  OneBitAdder onebitadder_2 (
    .CarryIn(onebitadder_3_carryout), .in1(not_2_out), .in2(1'b0), .Sum(Bit3Out),
    .CarryOut(onebitadder_2_carryout));
  not not_3 (not_3_out, Bit2In);
  OneBitAdder onebitadder_3 (
    .CarryIn(onebitadder_4_carryout), .in1(not_3_out), .in2(1'b0), .Sum(Bit2Out),
    .CarryOut(onebitadder_3_carryout));
  not not_4 (not_4_out, Bit1In);
  OneBitAdder onebitadder_4 (
    .CarryIn(1'b0), .in1(not_4_out), .in2(1'b1), .Sum(Bit1Out), .CarryOut(onebitadder_4_carryout));
endmodule

module ALU (
  input  L3in,
  input  L2in,
  input  L1in,
  input  L0in,
  input  R3in,
  input  R2in,
  input  R1in,
  input  R0in,
  input  ActiveClock,
  input  IsSubMode,
  output Negative,
  output Zero,
  output Overflow,
  output A3out,
  output A2out,
  output A1out,
  output A0out
);

  wire and_1_out, clock_1_out, controlled_buffer_1_out, controlled_buffer_2_out, controlled_buffer_5_out,
       controlled_buffer_7_out, controlled_buffer_9_out, controlled_buffer_10_out, controlled_buffer_12_out,
       controlled_buffer_14_out, controlled_buffer_15_out, controlled_buffer_16_out,
       controlled_buffer_19_out, controlled_buffer_20_out, newfourbitsnegativeb_1_bit1out,
       newfourbitsnegativeb_1_bit2out, newfourbitsnegativeb_1_bit3out, newfourbitsnegativeb_1_bit4out,
       not_1_out, not_2_out, not_3_out, not_4_out, not_5_out, not_6_out, onebitadder_1_carryout,
       onebitadder_2_carryout, onebitadder_3_carryout, onebitadder_4_carryout;

  not not_1 (not_1_out, ActiveClock);
  assign controlled_buffer_1_out = ActiveClock ? L3in : 1'bz;  // Controlled_Buffer controlled_buffer_1
  assign controlled_buffer_2_out = ActiveClock ? L2in : 1'bz;  // Controlled_Buffer controlled_buffer_2
  assign controlled_buffer_1_out = not_1_out ? 1'b0 : 1'bz;  // Controlled_Buffer controlled_buffer_3
  assign controlled_buffer_2_out = not_1_out ? 1'b0 : 1'bz;  // Controlled_Buffer controlled_buffer_4
  OneBitAdder onebitadder_1 (
    .CarryIn(onebitadder_2_carryout), .in1(controlled_buffer_10_out), .in2(controlled_buffer_1_out),
    .Sum(A3out), .CarryOut(onebitadder_1_carryout));
  // NoConnect on onebitadder_1_carryout
  assign controlled_buffer_5_out = ActiveClock ? L1in : 1'bz;  // Controlled_Buffer controlled_buffer_5
  assign controlled_buffer_5_out = not_1_out ? 1'b0 : 1'bz;  // Controlled_Buffer controlled_buffer_6
  assign controlled_buffer_7_out = ActiveClock ? L0in : 1'bz;  // Controlled_Buffer controlled_buffer_7
  assign controlled_buffer_7_out = not_1_out ? 1'b0 : 1'bz;  // Controlled_Buffer controlled_buffer_8
  OneBitAdder onebitadder_2 (
    .CarryIn(onebitadder_3_carryout), .in1(controlled_buffer_14_out), .in2(controlled_buffer_2_out),
    .Sum(A2out), .CarryOut(onebitadder_2_carryout));
  OneBitAdder onebitadder_3 (
    .CarryIn(onebitadder_4_carryout), .in1(controlled_buffer_19_out), .in2(controlled_buffer_5_out),
    .Sum(A1out), .CarryOut(onebitadder_3_carryout));
  OneBitAdder onebitadder_4 (
    .CarryIn(1'b0), .in1(controlled_buffer_20_out), .in2(controlled_buffer_7_out), .Sum(A0out),
    .CarryOut(onebitadder_4_carryout));
  assign controlled_buffer_9_out = not_1_out ? 1'b0 : 1'bz;  // Controlled_Buffer controlled_buffer_9
  assign controlled_buffer_10_out = not_2_out ? controlled_buffer_9_out : 1'bz;  // Controlled_Buffer controlled_buffer_10
  not not_2 (not_2_out, IsSubMode);
  assign controlled_buffer_9_out = ActiveClock ? R3in : 1'bz;  // Controlled_Buffer controlled_buffer_11
  assign controlled_buffer_12_out = ActiveClock ? R2in : 1'bz;  // Controlled_Buffer controlled_buffer_12
  assign controlled_buffer_12_out = not_1_out ? 1'b0 : 1'bz;  // Controlled_Buffer controlled_buffer_13
  assign controlled_buffer_14_out = not_2_out ? controlled_buffer_12_out : 1'bz;  // Controlled_Buffer controlled_buffer_14
  not not_3 (not_3_out, A3out);
  not not_4 (not_4_out, A2out);
  not not_5 (not_5_out, A1out);
  not not_6 (not_6_out, A0out);
  assign controlled_buffer_15_out = ActiveClock ? R0in : 1'bz;  // Controlled_Buffer controlled_buffer_15
  assign controlled_buffer_16_out = ActiveClock ? R1in : 1'bz;  // Controlled_Buffer controlled_buffer_16
  assign controlled_buffer_15_out = not_1_out ? 1'b0 : 1'bz;  // Controlled_Buffer controlled_buffer_17
  assign controlled_buffer_16_out = not_1_out ? 1'b0 : 1'bz;  // Controlled_Buffer controlled_buffer_18
  assign controlled_buffer_19_out = not_2_out ? controlled_buffer_16_out : 1'bz;  // Controlled_Buffer controlled_buffer_19
  assign controlled_buffer_20_out = not_2_out ? controlled_buffer_15_out : 1'bz;  // Controlled_Buffer controlled_buffer_20
  assign controlled_buffer_20_out = IsSubMode ? newfourbitsnegativeb_1_bit1out : 1'bz;  // Controlled_Buffer controlled_buffer_21
  Clock clock_1 (.out(clock_1_out));
  and and_1 (and_1_out, not_3_out, not_4_out, not_5_out, not_6_out);
  assign controlled_buffer_14_out = IsSubMode ? newfourbitsnegativeb_1_bit3out : 1'bz;  // Controlled_Buffer controlled_buffer_22
  assign controlled_buffer_19_out = IsSubMode ? newfourbitsnegativeb_1_bit2out : 1'bz;  // Controlled_Buffer controlled_buffer_23
  and and_2 (Zero, clock_1_out, and_1_out);
  OverFlowDetect overflowdetect_1 (
    .SignBitOfA(controlled_buffer_1_out), .SignBitOfB(controlled_buffer_10_out), .SignBitOfResult(A3out),
    .Overflow(Overflow));
  NewFourBitsNegativeB newfourbitsnegativeb_1 (
    .Bit4In(controlled_buffer_9_out), .Bit3In(controlled_buffer_12_out), .Bit2In(controlled_buffer_16_out),
    .Bit1In(controlled_buffer_15_out), .Bit4Out(newfourbitsnegativeb_1_bit4out),
    .Bit3Out(newfourbitsnegativeb_1_bit3out), .Bit2Out(newfourbitsnegativeb_1_bit2out),
    .Bit1Out(newfourbitsnegativeb_1_bit1out));
  assign controlled_buffer_10_out = IsSubMode ? newfourbitsnegativeb_1_bit4out : 1'bz;  // Controlled_Buffer controlled_buffer_24

  assign Negative = A3out;

  // Notes on the sheet:
  //   L input
  //   A-out output
  //   R input
endmodule

module DisplayScreenBlackbox (
  input  MSBBit,
  input  Bit2,
  input  Bit1,
  input  LSBBit,
  output D1B0345,
  output D1B12,
  output D1B6,
  output D2B0,
  output D2B1,
  output D2B2,
  output D2B3,
  output D2B4,
  output D2B5,
  output D2B6
);

  wire and_1_out, Eight_out, Eleven_out, Fifteen_out, Five_out, Four_out, Fourteen_out, not_1_out, not_2_out,
       not_3_out, One_out, Seven_out, Six_out, Ten_out, Thirteen_out, Three_out, Twelve_out, Two_out,
       Zero_out;

  and Zero (Zero_out, ~MSBBit, ~Bit2, ~Bit1, ~LSBBit);  // AND_Gate
  and One (One_out, ~MSBBit, ~Bit2, ~Bit1, LSBBit);  // AND_Gate
  and Two (Two_out, ~MSBBit, ~Bit2, Bit1, ~LSBBit);  // AND_Gate
  and Three (Three_out, ~MSBBit, ~Bit2, Bit1, LSBBit);  // AND_Gate
  and Four (Four_out, ~MSBBit, Bit2, ~Bit1, ~LSBBit);  // AND_Gate
  and Five (Five_out, ~MSBBit, Bit2, ~Bit1, LSBBit);  // AND_Gate
  and Six (Six_out, ~MSBBit, Bit2, Bit1, ~LSBBit);  // AND_Gate
  and Seven (Seven_out, ~MSBBit, Bit2, Bit1, LSBBit);  // AND_Gate
  and Eight (Eight_out, MSBBit, ~Bit2, ~Bit1, ~LSBBit);  // AND_Gate
  // AND_Gate Nine has open pins: in0=MSBBit, in1=Bit2, in2=Bit1, in3=LSBBit, out=open
  and Ten (Ten_out, MSBBit, ~Bit2, Bit1, ~LSBBit);  // AND_Gate
  and Eleven (Eleven_out, MSBBit, ~Bit2, Bit1, LSBBit);  // AND_Gate
  and Twelve (Twelve_out, MSBBit, Bit2, ~Bit1, ~LSBBit);  // AND_Gate
  and Thirteen (Thirteen_out, MSBBit, Bit2, ~Bit1, LSBBit);  // AND_Gate
  and Fourteen (Fourteen_out, MSBBit, Bit2, Bit1, ~LSBBit);  // AND_Gate
  and Fifteen (Fifteen_out, MSBBit, Bit2, Bit1, LSBBit);
  not not_1 (not_1_out, Bit1);
  not not_2 (not_2_out, Bit2);
  and and_1 (and_1_out, not_1_out, not_2_out, MSBBit);
  not not_3 (not_3_out, MSBBit);
  not not_4 (D1B6, 1'b1);
  or or_1 (D1B0345, and_1_out, not_3_out);
  and and_2 (D2B0, ~One_out, ~Four_out, ~Eleven_out, ~Fourteen_out);  // AND_Gate
  and and_3 (D2B1, ~Five_out, ~Six_out, ~Fifteen_out);  // AND_Gate
  and and_4 (D2B2, ~Two_out, ~Twelve_out);  // AND_Gate
  and and_5 (D2B3, ~One_out, ~Four_out, ~Seven_out, ~Eleven_out, ~Fourteen_out);  // AND_Gate
  or or_2 (D2B4, Zero_out, Two_out, Six_out, Eight_out, Ten_out, Twelve_out);
  and and_6 (D2B5, ~One_out, ~Two_out, ~Three_out, ~Seven_out, ~Eleven_out, ~Twelve_out, ~Thirteen_out);  // AND_Gate
  and and_7 (D2B6, ~Zero_out, ~One_out, ~Seven_out, ~Ten_out, ~Eleven_out);  // AND_Gate

  assign D1B12 = 1'b1;
endmodule

module MicroCounter (
  input  CounterClock,
  input  ResetToZero,
  output MicroZero,
  output MicroOne,
  output MicroTwo,
  output MicroThree,
  output MicroFour,
  output MicroFive,
  output MicroSix,
  output MicroSeven
);

  wire controlled_buffer_1_out, controlled_buffer_2_out, controlled_buffer_3_out, d_ff_1_q, d_ff_2_q,
       d_ff_3_q, FiveToSix_out, FourToFive_out, ModeAdd_out, ModeReset_out, not_1_out, not_2_out, not_3_out,
       not_4_out, not_5_out, not_6_out, not_7_out, not_8_out, not_9_out, not_10_out, not_11_out, not_12_out,
       not_13_out, OneToTwo_out, SevenToZero_out, SixToSeven_out, ThreeToFour_out, TwoToThree_out, undriven,
       undriven_2, ZeroToOne_out;

  not not_1 (not_1_out, ResetToZero);
  and ModeReset (ModeReset_out, CounterClock, ResetToZero);
  and ModeAdd (ModeAdd_out, CounterClock, not_1_out);
  assign controlled_buffer_1_out = ModeReset_out ? 1'b0 : 1'bz;  // Controlled_Buffer controlled_buffer_1
  assign controlled_buffer_2_out = ModeReset_out ? 1'b0 : 1'bz;  // Controlled_Buffer controlled_buffer_2
  assign controlled_buffer_3_out = ModeReset_out ? 1'b0 : 1'bz;  // Controlled_Buffer controlled_buffer_3
  and ZeroToOne (ZeroToOne_out, ModeAdd_out, MicroZero);
  assign controlled_buffer_3_out = ZeroToOne_out ? 1'b0 : 1'bz;  // Controlled_Buffer controlled_buffer_4
  assign controlled_buffer_2_out = ZeroToOne_out ? 1'b0 : 1'bz;  // Controlled_Buffer controlled_buffer_5
  assign controlled_buffer_1_out = ZeroToOne_out ? 1'b1 : 1'bz;  // Controlled_Buffer controlled_buffer_6
  and OneToTwo (OneToTwo_out, ModeAdd_out, MicroOne);
  assign controlled_buffer_3_out = OneToTwo_out ? 1'b0 : 1'bz;  // Controlled_Buffer controlled_buffer_7
  assign controlled_buffer_2_out = OneToTwo_out ? 1'b1 : 1'bz;  // Controlled_Buffer controlled_buffer_8
  assign controlled_buffer_1_out = OneToTwo_out ? 1'b0 : 1'bz;  // Controlled_Buffer controlled_buffer_9
  and TwoToThree (TwoToThree_out, ModeAdd_out, MicroTwo);
  D_Flip_Flop #(.trigger("falling")) d_ff_1 (
    .D(controlled_buffer_1_out), .clk(CounterClock), .Q(d_ff_1_q), .reset(undriven));  // open: Qn, preset
  D_Flip_Flop #(.trigger("falling")) d_ff_2 (
    .D(controlled_buffer_2_out), .clk(CounterClock), .Q(d_ff_2_q), .preset(undriven), .reset(undriven_2));  // open: Qn
  D_Flip_Flop #(.trigger("falling")) d_ff_3 (
    .D(controlled_buffer_3_out), .clk(CounterClock), .Q(d_ff_3_q), .preset(undriven_2));  // open: Qn, reset
  and ThreeToFour (ThreeToFour_out, ModeAdd_out, MicroThree);
  assign controlled_buffer_3_out = TwoToThree_out ? 1'b0 : 1'bz;  // Controlled_Buffer controlled_buffer_10
  assign controlled_buffer_2_out = TwoToThree_out ? 1'b1 : 1'bz;  // Controlled_Buffer controlled_buffer_11
  assign controlled_buffer_1_out = TwoToThree_out ? 1'b1 : 1'bz;  // Controlled_Buffer controlled_buffer_12
  and FourToFive (FourToFive_out, ModeAdd_out, MicroFour);
  assign controlled_buffer_3_out = ThreeToFour_out ? 1'b1 : 1'bz;  // Controlled_Buffer controlled_buffer_13
  assign controlled_buffer_2_out = ThreeToFour_out ? 1'b0 : 1'bz;  // Controlled_Buffer controlled_buffer_14
  assign controlled_buffer_1_out = ThreeToFour_out ? 1'b0 : 1'bz;  // Controlled_Buffer controlled_buffer_15
  assign controlled_buffer_3_out = FourToFive_out ? 1'b1 : 1'bz;  // Controlled_Buffer controlled_buffer_16
  assign controlled_buffer_2_out = FourToFive_out ? 1'b0 : 1'bz;  // Controlled_Buffer controlled_buffer_17
  assign controlled_buffer_1_out = FourToFive_out ? 1'b1 : 1'bz;  // Controlled_Buffer controlled_buffer_18
  and FiveToSix (FiveToSix_out, ModeAdd_out, MicroFive);
  assign controlled_buffer_3_out = FiveToSix_out ? 1'b1 : 1'bz;  // Controlled_Buffer controlled_buffer_19
  assign controlled_buffer_2_out = FiveToSix_out ? 1'b1 : 1'bz;  // Controlled_Buffer controlled_buffer_20
  assign controlled_buffer_1_out = FiveToSix_out ? 1'b0 : 1'bz;  // Controlled_Buffer controlled_buffer_21
  and SixToSeven (SixToSeven_out, ModeAdd_out, MicroSix);
  assign controlled_buffer_3_out = SixToSeven_out ? 1'b1 : 1'bz;  // Controlled_Buffer controlled_buffer_22
  assign controlled_buffer_2_out = SixToSeven_out ? 1'b1 : 1'bz;  // Controlled_Buffer controlled_buffer_23
  assign controlled_buffer_1_out = SixToSeven_out ? 1'b1 : 1'bz;  // Controlled_Buffer controlled_buffer_24
  and SevenToZero (SevenToZero_out, ModeAdd_out, MicroSeven);
  assign controlled_buffer_3_out = SevenToZero_out ? 1'b0 : 1'bz;  // Controlled_Buffer controlled_buffer_25
  assign controlled_buffer_2_out = SevenToZero_out ? 1'b0 : 1'bz;  // Controlled_Buffer controlled_buffer_26
  assign controlled_buffer_1_out = SevenToZero_out ? 1'b0 : 1'bz;  // Controlled_Buffer controlled_buffer_27
  and Seven (MicroSeven, d_ff_3_q, d_ff_2_q, d_ff_1_q);
  not not_2 (not_2_out, d_ff_1_q);
  not not_3 (not_3_out, d_ff_2_q);
  and Six (MicroSix, d_ff_3_q, d_ff_2_q, not_2_out);
  and Five (MicroFive, d_ff_3_q, not_3_out, d_ff_1_q);
  not not_4 (not_4_out, d_ff_2_q);
  not not_5 (not_5_out, d_ff_1_q);
  and Four (MicroFour, d_ff_3_q, not_4_out, not_5_out);
  not not_6 (not_6_out, d_ff_3_q);
  not not_7 (not_7_out, d_ff_3_q);
  and Three (MicroThree, not_6_out, d_ff_2_q, d_ff_1_q);
  not not_8 (not_8_out, d_ff_1_q);
  not not_9 (not_9_out, d_ff_3_q);
  not not_10 (not_10_out, d_ff_2_q);
  and Two (MicroTwo, not_7_out, d_ff_2_q, not_8_out);
  and One (MicroOne, not_9_out, not_10_out, d_ff_1_q);
  not not_11 (not_11_out, d_ff_3_q);
  not not_12 (not_12_out, d_ff_2_q);
  not not_13 (not_13_out, d_ff_1_q);
  and Zero (MicroZero, not_11_out, not_12_out, not_13_out);
endmodule
